# Fritzing sketch glockenspiel (saved by Fritzing 0.9.1b)
breadboards: 3

parts:
  Part1 = Arduino Mega 2560 (Rev3)
  J1 = female pin header, 3 pins [form="♀ (female)"]
  J3 = female pin header, 2 pins [form="♀ (female)"]
  D1 = Rectifier Diode [part_number=1N4004 package="300 mil [THT]"]
  R1 = Resistor [tolerance=±5% resistance=1k package=THT]
  C19 = Electrolytic Capacitor [capacitance=1000μF package="1010 [SMD, electrolytic]"]
  R2 = Resistor [tolerance=±5% resistance=1k package=THT]
  C20 = Electrolytic Capacitor [capacitance=1000μF package="1010 [SMD, electrolytic]"]
  J4 = female pin header, 3 pins [form="♀ (female)"]
  J5 = female pin header, 2 pins [form="♀ (female)"]
  D2 = Rectifier Diode [part_number=1N4004 package="300 mil [THT]"]
  R3 = Resistor [tolerance=±5% resistance=1k package=THT]
  C21 = Electrolytic Capacitor [capacitance=1000μF package="1010 [SMD, electrolytic]"]
  J6 = female pin header, 3 pins [form="♀ (female)"]
  J7 = female pin header, 2 pins [form="♀ (female)"]
  D3 = Rectifier Diode [part_number=1N4004 package="300 mil [THT]"]
  R4 = Resistor [tolerance=±5% resistance=1k package=THT]
  C22 = Electrolytic Capacitor [capacitance=1000μF package="1010 [SMD, electrolytic]"]
  J8 = female pin header, 3 pins [form="♀ (female)"]
  J9 = female pin header, 2 pins [form="♀ (female)"]
  D4 = Rectifier Diode [part_number=1N4004 package="300 mil [THT]"]
  R5 = Resistor [tolerance=±5% resistance=1k package=THT]
  C23 = Electrolytic Capacitor [capacitance=1000μF package="1010 [SMD, electrolytic]"]
  J10 = female pin header, 3 pins [form="♀ (female)"]
  J11 = female pin header, 2 pins [form="♀ (female)"]
  D5 = Rectifier Diode [part_number=1N4004 package="300 mil [THT]"]
  R6 = Resistor [tolerance=±5% resistance=1k package=THT]
  C24 = Electrolytic Capacitor [capacitance=1000μF package="1010 [SMD, electrolytic]"]
  J12 = female pin header, 3 pins [form="♀ (female)"]
  J13 = female pin header, 2 pins [form="♀ (female)"]
  D6 = Rectifier Diode [part_number=1N4004 package="300 mil [THT]"]
  R7 = Resistor [tolerance=±5% resistance=1k package=THT]
  C25 = Electrolytic Capacitor [capacitance=1000μF package="1010 [SMD, electrolytic]"]
  J14 = female pin header, 3 pins [form="♀ (female)"]
  J15 = female pin header, 2 pins [form="♀ (female)"]
  D7 = Rectifier Diode [part_number=1N4004 package="300 mil [THT]"]
  R8 = Resistor [tolerance=±5% resistance=1k package=THT]
  C26 = Electrolytic Capacitor [capacitance=1000μF package="1010 [SMD, electrolytic]"]
  J16 = female pin header, 3 pins [form="♀ (female)"]
  J17 = female pin header, 2 pins [form="♀ (female)"]
  D8 = Rectifier Diode [part_number=1N4004 package="300 mil [THT]"]
  R9 = Resistor [tolerance=±5% resistance=1k package=THT]
  C27 = Electrolytic Capacitor [capacitance=1000μF package="1010 [SMD, electrolytic]"]
  J18 = female pin header, 3 pins [form="♀ (female)"]
  J19 = female pin header, 2 pins [form="♀ (female)"]
  D9 = Rectifier Diode [part_number=1N4004 package="300 mil [THT]"]
  R10 = Resistor [tolerance=±5% resistance=1k package=THT]
  C28 = Electrolytic Capacitor [capacitance=1000μF package="1010 [SMD, electrolytic]"]
  J20 = female pin header, 3 pins [form="♀ (female)"]
  J21 = female pin header, 2 pins [form="♀ (female)"]
  D10 = Rectifier Diode [part_number=1N4004 package="300 mil [THT]"]
  R11 = Resistor [tolerance=±5% resistance=1k package=THT]
  C29 = Electrolytic Capacitor [capacitance=1000μF package="1010 [SMD, electrolytic]"]
  J22 = female pin header, 3 pins [form="♀ (female)"]
  J23 = female pin header, 2 pins [form="♀ (female)"]
  D11 = Rectifier Diode [part_number=1N4004 package="300 mil [THT]"]
  R12 = Resistor [tolerance=±5% resistance=1k package=THT]
  C30 = Electrolytic Capacitor [capacitance=1000μF package="1010 [SMD, electrolytic]"]
  J24 = female pin header, 3 pins [form="♀ (female)"]
  J25 = female pin header, 2 pins [form="♀ (female)"]
  D12 = Rectifier Diode [part_number=1N4004 package="300 mil [THT]"]
  R13 = Resistor [tolerance=±5% resistance=1k package=THT]
  C31 = Electrolytic Capacitor [capacitance=1000μF package="1010 [SMD, electrolytic]"]
  J26 = female pin header, 3 pins [form="♀ (female)"]
  J27 = female pin header, 2 pins [form="♀ (female)"]
  D13 = Rectifier Diode [part_number=1N4004 package="300 mil [THT]"]
  R14 = Resistor [tolerance=±5% resistance=1k package=THT]
  C32 = Electrolytic Capacitor [capacitance=1000μF package="1010 [SMD, electrolytic]"]
  J28 = female pin header, 3 pins [form="♀ (female)"]
  J29 = female pin header, 2 pins [form="♀ (female)"]
  D14 = Rectifier Diode [part_number=1N4004 package="300 mil [THT]"]
  R15 = Resistor [tolerance=±5% resistance=1k package=THT]
  C33 = Electrolytic Capacitor [capacitance=1000μF package="1010 [SMD, electrolytic]"]
  J30 = female pin header, 3 pins [form="♀ (female)"]
  J31 = female pin header, 2 pins [form="♀ (female)"]
  D15 = Rectifier Diode [part_number=1N4004 package="300 mil [THT]"]
  R16 = Resistor [tolerance=±5% resistance=1k package=THT]
  C34 = Electrolytic Capacitor [capacitance=1000μF package="1010 [SMD, electrolytic]"]
  J32 = female pin header, 3 pins [form="♀ (female)"]
  J33 = female pin header, 2 pins [form="♀ (female)"]
  D16 = Rectifier Diode [part_number=1N4004 package="300 mil [THT]"]
  R17 = Resistor [tolerance=±5% resistance=1k package=THT]
  C35 = Electrolytic Capacitor [capacitance=1000μF package="1010 [SMD, electrolytic]"]
  J34 = female pin header, 3 pins [form="♀ (female)"]
  J35 = female pin header, 2 pins [form="♀ (female)"]
  D17 = Rectifier Diode [part_number=1N4004 package="300 mil [THT]"]
  R18 = Resistor [tolerance=±5% resistance=1k package=THT]
  C36 = Electrolytic Capacitor [capacitance=1000μF package="1010 [SMD, electrolytic]"]
  J36 = female pin header, 3 pins [form="♀ (female)"]
  J37 = female pin header, 2 pins [form="♀ (female)"]
  D18 = Rectifier Diode [part_number=1N4004 package="300 mil [THT]"]
  R19 = Resistor [tolerance=±5% resistance=1k package=THT]
  C37 = Electrolytic Capacitor [capacitance=1000μF package="1010 [SMD, electrolytic]"]
  J38 = female pin header, 3 pins [form="♀ (female)"]
  J39 = female pin header, 2 pins [form="♀ (female)"]
  D19 = Rectifier Diode [part_number=1N4004 package="300 mil [THT]"]
  J40 = female pin header, 4 pins [form="♀ (female)"]
  J41 = female pin header, 4 pins [form="♀ (female)"]
  J42 = female pin header, 4 pins [form="♀ (female)"]
  J43 = female pin header, 4 pins [form="♀ (female)"]
  R20 = Resistor [tolerance=±5% resistance=220 package=THT]
  R21 = Resistor [tolerance=±5% resistance=220 package=THT]
  R22 = Resistor [tolerance=±5% resistance=220 package=THT]
  R23 = Resistor [tolerance=±5% resistance=220 package=THT]
  J44 = female pin header, 4 pins [form="♀ (female)"]
  R24 = Resistor [tolerance=±5% resistance=220 package=THT]

nets:
  N1: Part1.A14, J40.pin3
  N2: Part1.A15, R20.Pin_0
  N3: Part1.GND, J1.pin3, C19.-, C20.-, J4.pin3, C21.-, J6.pin3, C22.-, J8.pin3, C23.-, J10.pin3, C24.-, J12.pin3, C25.-, J14.pin3, C26.-, J16.pin3, C27.-, J18.pin3, C28.-, J20.pin3, C29.-, J22.pin3, C30.-, J24.pin3, C31.-, J26.pin3, C32.-, J28.pin3, C33.-, J30.pin3, C34.-, J32.pin3, C35.-, J34.pin3, C36.-, J36.pin3, C37.-, J38.pin3, J40.pin1, J40.pin4, J41.pin1, J41.pin4, J42.pin1, J42.pin4, J43.pin1, J43.pin4, J44.pin1, J44.pin4
  N4: Part1.VIN, J3.pin1, D1.cathode, C19.+, C20.+, J5.pin1, D2.cathode, C21.+, J7.pin1, D3.cathode, C22.+, J9.pin1, D4.cathode, C23.+, J11.pin1, D5.cathode, C24.+, J13.pin1, D6.cathode, C25.+, J15.pin1, D7.cathode, C26.+, J17.pin1, D8.cathode, C27.+, J19.pin1, D9.cathode, C28.+, J21.pin1, D10.cathode, C29.+, J23.pin1, D11.cathode, C30.+, J25.pin1, D12.cathode, C31.+, J27.pin1, D13.cathode, C32.+, J29.pin1, D14.cathode, C33.+, J31.pin1, D15.cathode, C34.+, J33.pin1, D16.cathode, C35.+, J35.pin1, D17.cathode, C36.+, J37.pin1, D18.cathode, C37.+, J39.pin1, D19.cathode
  N5: Part1.D22, R19.Pin_0
  N6: Part1.D23, R1.Pin_0
  N7: Part1.D24, R18.Pin_0
  N8: Part1.D25, R2.Pin_0
  N9: Part1.D26, R17.Pin_0
  N10: Part1.D27, R3.Pin_0
  N11: Part1.D28, R16.Pin_0
  N12: Part1.D29, R4.Pin_0
  N13: Part1.D30, R15.Pin_0
  N14: Part1.D31, R5.Pin_0
  N15: Part1.D32, R14.Pin_0
  N16: Part1.D33, R6.Pin_0
  N17: Part1.D34, R13.Pin_0
  N18: Part1.D35, R7.Pin_0
  N19: Part1.D36, R12.Pin_0
  N20: Part1.D37, R8.Pin_0
  N21: Part1.D38, R11.Pin_0
  N22: Part1.D39, R9.Pin_0
  N23: Part1.D41, R10.Pin_0
  N24: Part1.D42, J44.pin3
  N25: Part1.D43, R24.Pin_0
  N26: Part1.D44, J43.pin3
  N27: Part1.D45, R23.Pin_0
  N28: Part1.D46, J42.pin3
  N29: Part1.D47, R22.Pin_0
  N30: Part1.D48, J41.pin3
  N31: Part1.D49, R21.Pin_0
  N32: J1.pin1, R1.Pin_1
  N33: J1.pin2, J3.pin2, D1.anode
  N34: R2.Pin_1, J4.pin1
  N35: J4.pin2, J5.pin2, D2.anode
  N36: R3.Pin_1, J6.pin1
  N37: J6.pin2, J7.pin2, D3.anode
  N38: R4.Pin_1, J8.pin1
  N39: J8.pin2, J9.pin2, D4.anode
  N40: R5.Pin_1, J10.pin1
  N41: J10.pin2, J11.pin2, D5.anode
  N42: R6.Pin_1, J12.pin1
  N43: J12.pin2, J13.pin2, D6.anode
  N44: R7.Pin_1, J14.pin1
  N45: J14.pin2, J15.pin2, D7.anode
  N46: R8.Pin_1, J16.pin1
  N47: J16.pin2, J17.pin2, D8.anode
  N48: R9.Pin_1, J18.pin1
  N49: J18.pin2, J19.pin2, D9.anode
  N50: R10.Pin_1, J20.pin1
  N51: J20.pin2, J21.pin2, D10.anode
  N52: R11.Pin_1, J22.pin1
  N53: J22.pin2, J23.pin2, D11.anode
  N54: R12.Pin_1, J24.pin1
  N55: J24.pin2, J25.pin2, D12.anode
  N56: R13.Pin_1, J26.pin1
  N57: J26.pin2, J27.pin2, D13.anode
  N58: R14.Pin_1, J28.pin1
  N59: J28.pin2, J29.pin2, D14.anode
  N60: R15.Pin_1, J30.pin1
  N61: J30.pin2, J31.pin2, D15.anode
  N62: R16.Pin_1, J32.pin1
  N63: J32.pin2, J33.pin2, D16.anode
  N64: R17.Pin_1, J34.pin1
  N65: J34.pin2, J35.pin2, D17.anode
  N66: R18.Pin_1, J36.pin1
  N67: J36.pin2, J37.pin2, D18.anode
  N68: R19.Pin_1, J38.pin1
  N69: J38.pin2, J39.pin2, D19.anode
  N70: J40.pin2, R20.Pin_1
  N71: J41.pin2, R21.Pin_1
  N72: J42.pin2, R22.Pin_1
  N73: J43.pin2, R23.Pin_1
  N74: J44.pin2, R24.Pin_1

notes:
  3-connector = TIP120
  Pin order: B C E
  2 connector = solenoid
  See MechanicalNotes.odp for wiring of these lighted button connectors
  Button connector order: On/Off, Play/Pause, Back, Forward, Shuffle
